# Fritzing sketch samogon.ESP-D1-mini (saved by Fritzing 0.9.4)

parts:
  DS18B20 = DS18B20 1-Wire Temperature Sensor
  R1 = Resistor [tolerance=±5% resistance=4.7k package=THT]
  WeMos_D1_Mini1 = WeMos D1 Mini

nets:
  N1: DS18B20.GND, WeMos_D1_Mini1.G
  N2: DS18B20.DQ, R1.Pin_0, WeMos_D1_Mini1.D3
  VDD: DS18B20.VDD, R1.Pin_1, WeMos_D1_Mini1.5V
