# Fritzing sketch samogon (saved by Fritzing 0.9.4)

parts:
  WeMos_D1_Mini_WS2812B_RGB_Shield1 = WeMos D1 Mini WS2812B RGB Shield
  HLK-PM1 = HLK-PM01
  DS1 = DS18B20 1-Wire Temperature Sensor [part_number=DS18B20]
  J1 = Piezo Speaker
  U1 = RELAY [package=relay-t9a-2]
  Q1 = TRANSISTOR_NPN [package=to-92-ammo]

nets:
  3V3: WeMos_D1_Mini_WS2812B_RGB_Shield1.3V3, HLK-PM1.+Vo, DS1.VDD, U1.COIL2
  N1: WeMos_D1_Mini_WS2812B_RGB_Shield1.D0, J1.pin2
  N2: WeMos_D1_Mini_WS2812B_RGB_Shield1.D1, Q1.B
  N3: WeMos_D1_Mini_WS2812B_RGB_Shield1.D3, DS1.DQ
  N4: WeMos_D1_Mini_WS2812B_RGB_Shield1.G, HLK-PM1.-Vo, DS1.GND, J1.pin1, Q1.E
  N5: U1.COIL1, Q1.C
